# Fritzing sketch RemoteShematic (saved by Fritzing 1.0.4)
breadboards: 1

parts:
  Joystick1 = Black Joystick KY-023
  Transmitter1 = nRF24L01 [package=module]
  Robot_Controller1 = Arduino Nano (Rev3.0)
  VCC3 = Battery block 9V [internal_resistance=0.1Ω]
  C3 = Capacitor Polarized [package=cpol-radial-100uf-25v]
  S1 = Toggle Switch [package=THT]

nets:
  N1: Joystick1.SW, Robot_Controller1.D2
  N2: Joystick1.VRy, Robot_Controller1.A0
  N3: Joystick1.VRx, Robot_Controller1.A1
  +5V: Joystick1.+5V, Robot_Controller1.5V
  GND: Joystick1.GND, Transmitter1.GND, VCC3.-, C3.-
  VCC: Transmitter1.VCC, Robot_Controller1.3V3, C3.+
  N4: Transmitter1.CE, Robot_Controller1.D7
  N5: Transmitter1.CSN, Robot_Controller1.D8
  N6: Transmitter1.SCK, Robot_Controller1.D13/SCK
  N7: Transmitter1.MOSI, Robot_Controller1.D11/MOSI
  N8: Transmitter1.MISO, Robot_Controller1.D12/MISO
  N9: Robot_Controller1.VIN, S1.COM
  N10: VCC3.+, S1.L1

custom parts:
  Black Joystick KY-023: Description: The joystick is a combination of 2 analoog potentiometer and a digital switch. Arduino GND --> Module pin - Arduino +5V --> Module pin +5V Arduino Analoog 0 --> Module VRx Arduino Analoog 1 --> Module VRy Arduino Digital --> Module SW Dimensions: 1" x 1.25"
  nRF24L01: nRF24L01 module
