# Fritzing sketch RobotSchematic (saved by Fritzing 1.0.4)
breadboards: 1

parts:
  Part6 = Motor Driver 1A Dual TB6612FNG
  Right1 = gear-motor
  Left1 = gear-motor
  Receiver1 = nRF24L01 [package=module]
  Part7 = Arduino Nano (Rev3.0)
  VCC2 = Battery block 9V [internal_resistance=0.1Ω]
  C2 = Capacitor Polarized [package=cpol-radial-100uf-25v]
  S1 = Toggle Switch [package=THT]  # not connected

nets:
  GND: Part6.GND, Receiver1.GND, VCC2.-, C2.-
  N1: Part6.B01, Right1.pin_1
  N2: Part6.B02, Right1.pin_2
  N3: Part6.A02, Left1.pin_2
  N4: Part6.A01, Left1.pin_1
  VCC: Part6.VCC, Part6.VM, Part6.STBY, Part7.5V
  N5: Part6.PWMA, Part7.D3
  N6: Part6.AIN2, Part7.D4
  N7: Part6.AIN1, Part7.D2
  N8: Part6.BIN1, Part7.D6
  N9: Part6.BIN2, Part7.D9
  N10: Part6.PWMB, Part7.D5
  VCC_2: Receiver1.VCC, Part7.3V3, C2.+
  N11: Receiver1.CE, Part7.D7
  N12: Receiver1.CSN, Part7.D8
  N13: Receiver1.SCK, Part7.D13/SCK
  N14: Receiver1.MOSI, Part7.D11/MOSI
  N15: Receiver1.MISO, Part7.D12/MISO

custom parts:
  nRF24L01: nRF24L01 module
